# Fritzing sketch Schematics (saved by Fritzing 0.9.2b)
breadboards: 3

parts:
  Raspberry_Pi1 = Raspberry Pi 2  # not connected
  Part1 = Arduino Uno (Rev3)
  Part2 = Arduino Uno (Rev3)
  Part4 = Arduino Uno (Rev3)  # not connected
  S1 = Pushbutton [package="[THT]"]
  S2 = Pushbutton [package="[THT]"]
  S3 = Pushbutton [package="[THT]"]
  S4 = Pushbutton [package="[THT]"]
  S5 = Pushbutton [package="[THT]"]
  S6 = Pushbutton [package="[THT]"]
  S7 = Pushbutton [package="[THT]"]
  S8 = Pushbutton [package="[THT]"]
  Part5 = Arduino Uno (Rev3)  # not connected
  KY-1 = Keyes Relay [package=THT]
  L1 = Solenoid
  Part3 = Arduino Uno (Rev3)
  KY-2 = Keyes Relay [package=THT]
  L2 = Solenoid
  J1 = Basic Servo
  M1 = DC Motor
  Part6 = Arduino Motor Shield (Rev3)
  Part7 = Arduino Motor Shield (Rev3)
  Power_plug1 = Power plug

nets:
  N1: Part1.D8, S4.Pin_1, S4.Pin_2
  N2: Part1.D9_PWM, S3.Pin_1, S3.Pin_2
  N3: Part1.D11_PWM/MOSI, Part2.D0/RX
  N4: Part1.D12/MISO, S2.Pin_1, S2.Pin_2
  N5: Part1.D13/SCK, S1.Pin_1, S1.Pin_2
  N6: Part1.D4, S8.Pin_1, S8.Pin_2
  N7: Part1.D5_PWM, S7.Pin_1, S7.Pin_2
  N8: Part1.D6_PWM, S6.Pin_1, S6.Pin_2
  N9: Part1.D7, S5.Pin_1, S5.Pin_2
  N10: Part1.GND, S1.Pin_3, S1.Pin_4, S2.Pin_3, S2.Pin_4, S3.Pin_3, S3.Pin_4, S4.Pin_3, S4.Pin_4, S5.Pin_3, S5.Pin_4, S6.Pin_3, S6.Pin_4, S7.Pin_3, S7.Pin_4, S8.Pin_3, S8.Pin_4
  N11: Part2.D13/SCK, KY-1.signal
  N12: Part2.D1/TX, Part3.D0/RX
  N13: Part2.5V, KY-1.power
  N14: Part2.GND, KY-1.ground
  N15: KY-1.C, KY-2.C, Power_plug1.GND
  N16: KY-1.NO, L1.pin1
  N17: L1.pin2, L2.pin2, Power_plug1.VCC
  N18: Part3.D1/TX, Part6.IOREF
  N19: Part3.5V, KY-2.power
  N20: Part3.GND, KY-2.ground
  N21: KY-2.NO, L2.pin1
  GND: J1.gnd, Part6.GND
  VCC: J1.vcc, Part6.5V
  N22: J1.pulse, Part6.D6_PWM
  N23: M1.pin_1, Part7.B+
  N24: M1.pin_2, Part7.B-
  N25: Part6.D1/TX, Part7.IOREF

notes:
  Master
  Each button represents a component (solenoid, dc motor etc) on the arduino chain. A button press sends the component key to the Rasp Pi via serial.
  When a key is received via serial, it's sent forward via software serial.
  Solenoid 1
  Keys: A-H
  Solenoid 2
  Keys: I-P
  Motor shield 1
  Keys: Q-V
  Motor shield 2
  Keys: W-Z
  Rasp PI is running the PD patch
  All Arduinos must share ground (for example powered witht the same power source)

custom parts:
  Keyes Relay: The Keyes 5V relay module is suitable for SCM development, home appliance control. It uses a 5V~12V TIL control signal which can control DC / AC signal.
